// Logisim project Slide10_Reg_FF_D_CargaParalela - 4 bits (atividade).circ as structural Verilog: 2 circuits, main circuit main
module main (
);

  Register #(.width(4), .trigger("falling"), .Select("low")) register_1 ();  // open: D, en, Q, clk, clr
  reg_paralelo reg_paralelo_1 ();  // open: CLK, out_6, out_7, out_8, out_9, in_2, in_3, in_4, in_5
endmodule

module reg_paralelo (
  input  CLK,
  input  in_2,
  input  in_3,
  input  in_4,
  input  in_5,
  output out_6,
  output out_7,
  output out_8,
  output out_9
);

  D_Flip_Flop #(.trigger("falling")) d_ff_1 (.clk(CLK), .D(in_2), .Q(out_6));  // open: Qn, preset, reset
  D_Flip_Flop #(.trigger("falling")) d_ff_2 (.clk(CLK), .D(in_3), .Q(out_7));  // open: Qn, preset, reset
  D_Flip_Flop #(.trigger("falling")) d_ff_3 (.clk(CLK), .D(in_4), .Q(out_8));  // open: Qn, preset, reset
  D_Flip_Flop #(.trigger("falling")) d_ff_4 (.clk(CLK), .D(in_5), .Q(out_9));  // open: Qn, preset, reset

  // Notes on the sheet:
  //   Ativo em borda de descida, então quando o clk está em 0 é que a informacão dos inputs é transferida para os outputs
endmodule
