// Logisim project xor.circ as structural Verilog: 1 circuit, main circuit main
// XOR
module main (
  input  X,
  input  Y,
  output XOR
);

  wire and_1_out, and_2_out, not_1_out, not_2_out;

  not not_1 (not_1_out, X);
  and and_1 (and_1_out, not_1_out, Y);
  and and_2 (and_2_out, X, not_2_out);
  not not_2 (not_2_out, Y);
  or or_1 (XOR, and_1_out, and_2_out);
endmodule
