// Logisim project Slide20_ContFF_T_Sincrono(aula-8bits).circ as structural Verilog: 1 circuit, main circuit main
module main (
);

  wire and_1_out, CLK_out;
  wire [2:0] t_ff_1_q;

  Clock CLK (.out(CLK_out));
  T_Flip_Flop #(.NegatePresetClear("true")) t_ff_1 (
    .clk(CLK_out), .T(1'b1), .Q(t_ff_1_q[0]));  // open: Qn, preset, reset
  Hex_Digit_Display hex_digit_display_1 (.value({1'b0, t_ff_1_q}));  // open: dp
  T_Flip_Flop #(.NegatePresetClear("true")) t_ff_2 (
    .clk(CLK_out), .T(t_ff_1_q[0]), .Q(t_ff_1_q[1]));  // open: Qn, preset, reset
  and and_1 (and_1_out, t_ff_1_q[1], t_ff_1_q[0]);
  T_Flip_Flop #(.NegatePresetClear("true")) t_ff_3 (
    .clk(CLK_out), .T(and_1_out), .Q(t_ff_1_q[2]));  // open: Qn, preset, reset

  // Notes on the sheet:
  //   Q0
  //   Q1
  //   Q2
endmodule
