// Logisim project Slide14_Memoria.circ as structural Verilog: 1 circuit, main circuit main
module main (
  input  [3:0] \Endereços ,
  output [7:0] Dados
);

  wire dipswitch_1_p1;

  Hex_Digit_Display hex_digit_display_1 (.value(\Endereços ));  // open: dp
  // DipSwitch #(.NSwitches(1)) dipswitch_1: pin names not known; wires that end beside it: dipswitch_1_p1
  Hex_Digit_Display hex_digit_display_2 (.value(Dados[3:0]));  // open: dp
  Hex_Digit_Display hex_digit_display_3 (.value(Dados[7:4]));  // open: dp
  ROM #(.addrWidth(4)) rom_1 (.addr(\Endereços ), .data(Dados), .sel(dipswitch_1_p1));

  // Notes on the sheet:
  //   contents of rom_1 (hex, n*v repeats v):
  //   ae ba bb ab b3 bf ab ba ba a2 bc b9 a8 b9 b0 ad
endmodule
