// Logisim project Slide16_Memoria_16Reg8.circ as structural Verilog: 1 circuit, main circuit main
module main (
  output [3:0] \Endereço 
);

  wire and_1_out, and_2_out, and_3_out, and_4_out, and_5_out, and_6_out, and_7_out, and_8_out, and_9_out,
       and_10_out, and_11_out, and_12_out, and_13_out, and_14_out, and_15_out, and_16_out, clock_1_out,
       demultiplexer_1_out0, demultiplexer_1_out1, demultiplexer_1_out2, demultiplexer_1_out3,
       demultiplexer_2_out0, demultiplexer_2_out1, demultiplexer_2_out2, demultiplexer_2_out3;
  wire [3:0] controlled_buffer_1_out, controlled_buffer_1_out_2;
  wire [7:0] Reg_0_q, Reg_1_q, Reg_2_q, Reg_3_q, Reg_4_q, Reg_5_q, Reg_6_q, Reg_7_q, Reg_8_q, Reg_9_q,
       Reg_10_q, Reg_11_q, Reg_12_q, Reg_13_q, Reg_14_q, Reg_15_q;

  // DipSwitch A3_A2_A1_A0: pin names not known; wires that end beside it: \Endereço [3], \Endereço [2], \Endereço [1], 1'b1, \Endereço [0]
  Demultiplexer #(.select(2), .enable("false")) demultiplexer_1 (
    .out0(demultiplexer_1_out0), .out1(demultiplexer_1_out1), .out2(demultiplexer_1_out2),
    .out3(demultiplexer_1_out3), .in(1'b1), .sel(\Endereço [1:0]));
  Clock clock_1 (.out(clock_1_out));
  Demultiplexer #(.select(2), .enable("false")) demultiplexer_2 (
    .out0(demultiplexer_2_out0), .out1(demultiplexer_2_out1), .out2(demultiplexer_2_out2),
    .out3(demultiplexer_2_out3), .in(1'b1), .sel(\Endereço [3:2]));
  Hex_Digit_Display hex_digit_display_1 (.value(controlled_buffer_1_out));  // open: dp
  Hex_Digit_Display hex_digit_display_2 (.value(controlled_buffer_1_out_2));  // open: dp
  LED led_1 (.in(and_1_out));
  and and_1 (and_1_out, demultiplexer_1_out0, demultiplexer_2_out0);
  Register #(.Select("high")) Reg_0 (
    .D({8{1'b0}}), .Q(Reg_0_q), .clk(clock_1_out), .cs(and_1_out));  // open: en, clr, preset
  LED led_2 (.in(and_2_out));
  and and_2 (and_2_out, demultiplexer_1_out1, demultiplexer_2_out0);
  LED led_3 (.in(and_3_out));
  and and_3 (and_3_out, demultiplexer_1_out2, demultiplexer_2_out0);
  and and_4 (and_4_out, demultiplexer_1_out3, demultiplexer_2_out0);
  assign {controlled_buffer_1_out_2, controlled_buffer_1_out} = and_1_out ? Reg_0_q : 8'bz;  // Controlled_Buffer controlled_buffer_1
  assign {controlled_buffer_1_out_2, controlled_buffer_1_out} = and_2_out ? Reg_1_q : 8'bz;  // Controlled_Buffer controlled_buffer_2
  Register #(.Select("high")) Reg_1 (
    .D(8'h1), .Q(Reg_1_q), .clk(clock_1_out), .cs(and_2_out));  // open: en, clr, preset
  assign {controlled_buffer_1_out_2, controlled_buffer_1_out} = and_3_out ? Reg_2_q : 8'bz;  // Controlled_Buffer controlled_buffer_3
  Register #(.Select("high")) Reg_2 (
    .D(8'h2), .Q(Reg_2_q), .clk(clock_1_out), .cs(and_3_out));  // open: en, clr, preset
  assign {controlled_buffer_1_out_2, controlled_buffer_1_out} = and_4_out ? Reg_3_q : 8'bz;  // Controlled_Buffer controlled_buffer_4
  LED led_4 (.in(and_4_out));
  Register #(.Select("high")) Reg_3 (
    .D(8'h3), .Q(Reg_3_q), .clk(clock_1_out), .cs(and_4_out));  // open: en, clr, preset
  LED led_5 (.in(and_5_out));
  and and_5 (and_5_out, demultiplexer_1_out0, demultiplexer_2_out1);
  and and_6 (and_6_out, demultiplexer_1_out1, demultiplexer_2_out1);
  assign {controlled_buffer_1_out_2, controlled_buffer_1_out} = and_5_out ? Reg_4_q : 8'bz;  // Controlled_Buffer controlled_buffer_5
  Register #(.Select("high")) Reg_4 (
    .D(8'h4), .Q(Reg_4_q), .clk(clock_1_out), .cs(and_5_out));  // open: en, clr, preset
  assign {controlled_buffer_1_out_2, controlled_buffer_1_out} = and_6_out ? Reg_5_q : 8'bz;  // Controlled_Buffer controlled_buffer_6
  LED led_6 (.in(and_6_out));
  Register #(.Select("high")) Reg_5 (
    .D(8'h5), .Q(Reg_5_q), .clk(clock_1_out), .cs(and_6_out));  // open: en, clr, preset
  LED led_7 (.in(and_7_out));
  and and_7 (and_7_out, demultiplexer_1_out2, demultiplexer_2_out1);
  Register #(.Select("high")) Reg_6 (
    .D(8'h6), .Q(Reg_6_q), .clk(clock_1_out), .cs(and_7_out));  // open: en, clr, preset
  LED led_8 (.in(and_8_out));
  and and_8 (and_8_out, demultiplexer_1_out3, demultiplexer_2_out1);
  assign {controlled_buffer_1_out_2, controlled_buffer_1_out} = and_7_out ? Reg_6_q : 8'bz;  // Controlled_Buffer controlled_buffer_7
  assign {controlled_buffer_1_out_2, controlled_buffer_1_out} = and_8_out ? Reg_7_q : 8'bz;  // Controlled_Buffer controlled_buffer_8
  Register #(.Select("high")) Reg_7 (
    .D(8'h7), .Q(Reg_7_q), .clk(clock_1_out), .cs(and_8_out));  // open: en, clr, preset
  LED led_9 (.in(and_9_out));
  and and_9 (and_9_out, demultiplexer_1_out0, demultiplexer_2_out2);
  Register #(.Select("high")) Reg_8 (
    .D(8'h8), .Q(Reg_8_q), .clk(clock_1_out), .cs(and_9_out));  // open: en, clr, preset
  LED led_10 (.in(and_10_out));
  and and_10 (and_10_out, demultiplexer_1_out1, demultiplexer_2_out2);
  LED led_11 (.in(and_11_out));
  and and_11 (and_11_out, demultiplexer_1_out2, demultiplexer_2_out2);
  and and_12 (and_12_out, demultiplexer_1_out3, demultiplexer_2_out2);
  assign {controlled_buffer_1_out_2, controlled_buffer_1_out} = and_9_out ? Reg_8_q : 8'bz;  // Controlled_Buffer controlled_buffer_9
  assign {controlled_buffer_1_out_2, controlled_buffer_1_out} = and_10_out ? Reg_9_q : 8'bz;  // Controlled_Buffer controlled_buffer_10
  Register #(.Select("high")) Reg_9 (
    .D(8'h9), .Q(Reg_9_q), .clk(clock_1_out), .cs(and_10_out));  // open: en, clr, preset
  assign {controlled_buffer_1_out_2, controlled_buffer_1_out} = and_11_out ? Reg_10_q : 8'bz;  // Controlled_Buffer controlled_buffer_11
  Register #(.Select("high")) Reg_10 (
    .D(8'ha), .Q(Reg_10_q), .clk(clock_1_out), .cs(and_11_out));  // open: en, clr, preset
  assign {controlled_buffer_1_out_2, controlled_buffer_1_out} = and_12_out ? Reg_11_q : 8'bz;  // Controlled_Buffer controlled_buffer_12
  LED led_12 (.in(and_12_out));
  Register #(.Select("high")) Reg_11 (
    .D(8'hb), .Q(Reg_11_q), .clk(clock_1_out), .cs(and_12_out));  // open: en, clr, preset
  LED led_13 (.in(and_13_out));
  and and_13 (and_13_out, demultiplexer_1_out0, demultiplexer_2_out3);
  and and_14 (and_14_out, demultiplexer_1_out1, demultiplexer_2_out3);
  assign {controlled_buffer_1_out_2, controlled_buffer_1_out} = and_13_out ? Reg_12_q : 8'bz;  // Controlled_Buffer controlled_buffer_13
  Register #(.Select("high")) Reg_12 (
    .D(8'hc), .Q(Reg_12_q), .clk(clock_1_out), .cs(and_13_out));  // open: en, clr, preset
  assign {controlled_buffer_1_out_2, controlled_buffer_1_out} = and_14_out ? Reg_13_q : 8'bz;  // Controlled_Buffer controlled_buffer_14
  LED led_14 (.in(and_14_out));
  Register #(.Select("high")) Reg_13 (
    .D(8'hd), .Q(Reg_13_q), .clk(clock_1_out), .cs(and_14_out));  // open: en, clr, preset
  LED led_15 (.in(and_15_out));
  and and_15 (and_15_out, demultiplexer_1_out2, demultiplexer_2_out3);
  Register #(.Select("high")) Reg_14 (
    .D(8'he), .Q(Reg_14_q), .clk(clock_1_out), .cs(and_15_out));  // open: en, clr, preset
  LED led_16 (.in(and_16_out));
  and and_16 (and_16_out, demultiplexer_1_out3, demultiplexer_2_out3);
  assign {controlled_buffer_1_out_2, controlled_buffer_1_out} = and_15_out ? Reg_14_q : 8'bz;  // Controlled_Buffer controlled_buffer_15
  assign {controlled_buffer_1_out_2, controlled_buffer_1_out} = and_16_out ? Reg_15_q : 8'bz;  // Controlled_Buffer controlled_buffer_16
  Register #(.Select("high")) Reg_15 (
    .D(8'hf), .Q(Reg_15_q), .clk(clock_1_out), .cs(and_16_out));  // open: en, clr, preset

  // Notes on the sheet:
  //   Linhas
  //   Colunas
  //   Linha 0
  //   Linha 1
  //   Linha 2
  //   Linha 3
  //   Coluna 0
  //   Coluna 1
  //   Coluna 2
  //   Coluna 3
endmodule
