// Logisim project CPU_Contador_Memoria_1.3.circ as structural Verilog: 7 circuits, main circuit CPU
// CLK
module CPU (
);

  wire K0, K1, K2, K3, L8, L9, S0, S1, S2, S3, S4, S5, S6, S7, S8, S9;
  wire [3:0] HEX0, HEX1, HEX2, HEX3, HEX4, HEX5;
  wire [7:0] A1;

  Hex_Digit_Display hex_digit_display_1 (.value(HEX5));  // open: dp
  LED u_L8 (.in(L8));
  LED u_L9 (.in(L9));
  // DipSwitch #(.NSwitches(1)) S8: pin names not known; wires that end beside it: S8
  // DipSwitch #(.NSwitches(1)) S9: pin names not known; wires that end beside it: S9
  // Digital_Oscilloscope digital_oscilloscope_1: pin names not known; wires that end beside it: S9, A1[0], A1[1], A1[2], A1[3], A1[4], A1[5], A1[6], A1[7], K0
  Hex_Digit_Display hex_digit_display_2 (.value(HEX4));  // open: dp
  Hex_Digit_Display hex_digit_display_3 (.value(HEX3));  // open: dp
  LED L6 (.in(A1[6]));
  LED L7 (.in(A1[7]));
  LED L5 (.in(A1[5]));
  // DipSwitch #(.NSwitches(1)) S6: pin names not known; wires that end beside it: S6
  // DipSwitch #(.NSwitches(1)) S5: pin names not known; wires that end beside it: S5
  // DipSwitch #(.NSwitches(1)) S7: pin names not known; wires that end beside it: S7
  Hex_Digit_Display hex_digit_display_4 (.value(HEX2));  // open: dp
  LED L3 (.in(A1[3]));
  LED L4 (.in(A1[4]));
  // DipSwitch #(.NSwitches(1)) S2: pin names not known; wires that end beside it: S2
  // DipSwitch #(.NSwitches(1)) S3: pin names not known; wires that end beside it: S3
  // DipSwitch #(.NSwitches(1)) S4: pin names not known; wires that end beside it: S4
  Hex_Digit_Display hex_digit_display_5 (.value(HEX1));  // open: dp
  Hex_Digit_Display hex_digit_display_6 (.value(HEX0));  // open: dp
  LED L1 (.in(A1[1]));
  LED L2 (.in(A1[2]));
  LED L0 (.in(A1[0]));
  // DipSwitch #(.NSwitches(1)) S1: pin names not known; wires that end beside it: S1
  // DipSwitch #(.NSwitches(1)) M_CLR: pin names not known; wires that end beside it: S0, A1[0]
  Button u_K3 (.out(K3));
  Button u_K2 (.out(K2));
  Button Reset2 (.out(K1));
  Button Reset1 (.out(K0));
  Contador_Sincrono contador_sincrono_1 (.CLK(S9), .CLEAR(S0), .out_3(A1));
  ROM #(.dataWidth(16), .Select("low")) rom_1 (.addr(A1), .data({HEX5, HEX4, HEX3, HEX2}));

  // Other names for the same wires on the sheet: L0 = A1[0]; L1 = A1[1]; L2 = A1[2]; L3 = A1[3]; L4 = A1[4];
  //   L5 = A1[5]; L6 = A1[6]; L7 = A1[7]

  // Notes on the sheet:
  //   contents of rom_1 (hex, n*v repeats v):
  //   10 0 0 1 1 1 0 1 10 10 0 10 10 11 22*0 10 0 0 1 1 0 0 1 1 0 0 10 10 11 0 10 10 1 0 10 1 11 0 10 10
  //   10 0 0 10 0 0 1
endmodule

module Memoria (
  input  [15:0] in_1,
  input  CLK,
  input  LOAD,
  output [15:0] out_4
);

  wire multiplexer_1_out, multiplexer_2_out, multiplexer_3_out, multiplexer_4_out, multiplexer_5_out,
       multiplexer_6_out, multiplexer_7_out, multiplexer_8_out, multiplexer_9_out, multiplexer_10_out,
       multiplexer_11_out, multiplexer_12_out, multiplexer_13_out, multiplexer_14_out, multiplexer_15_out,
       multiplexer_16_out;

  Multiplexer #(.enable("false")) multiplexer_1 (.in0(out_4[0]), .in1(in_1[0]), .out(multiplexer_1_out), .sel(LOAD));
  D_Flip_Flop #(.trigger("falling")) d_ff_1 (
    .clk(CLK), .D(multiplexer_1_out), .Q(out_4[0]));  // open: Qn, preset, reset
  Multiplexer #(.enable("false")) multiplexer_2 (.in0(out_4[1]), .in1(in_1[1]), .out(multiplexer_2_out), .sel(LOAD));
  D_Flip_Flop #(.trigger("falling")) d_ff_2 (
    .clk(CLK), .D(multiplexer_2_out), .Q(out_4[1]));  // open: Qn, preset, reset
  Multiplexer #(.enable("false")) multiplexer_3 (.in0(out_4[2]), .in1(in_1[2]), .out(multiplexer_3_out), .sel(LOAD));
  D_Flip_Flop #(.trigger("falling")) d_ff_3 (
    .clk(CLK), .D(multiplexer_3_out), .Q(out_4[2]));  // open: Qn, preset, reset
  D_Flip_Flop #(.trigger("falling")) d_ff_4 (
    .clk(CLK), .D(multiplexer_4_out), .Q(out_4[3]));  // open: Qn, preset, reset
  Multiplexer #(.enable("false")) multiplexer_4 (.in0(out_4[3]), .in1(in_1[3]), .out(multiplexer_4_out), .sel(LOAD));
  D_Flip_Flop #(.trigger("falling")) d_ff_5 (
    .clk(CLK), .D(multiplexer_5_out), .Q(out_4[4]));  // open: Qn, preset, reset
  Multiplexer #(.enable("false")) multiplexer_5 (.in0(out_4[4]), .in1(in_1[4]), .out(multiplexer_5_out), .sel(LOAD));
  Multiplexer #(.enable("false")) multiplexer_6 (.in0(out_4[5]), .in1(in_1[5]), .out(multiplexer_6_out), .sel(LOAD));
  D_Flip_Flop #(.trigger("falling")) d_ff_6 (
    .clk(CLK), .D(multiplexer_6_out), .Q(out_4[5]));  // open: Qn, preset, reset
  Multiplexer #(.enable("false")) multiplexer_7 (.in0(out_4[6]), .in1(in_1[6]), .out(multiplexer_7_out), .sel(LOAD));
  D_Flip_Flop #(.trigger("falling")) d_ff_7 (
    .clk(CLK), .D(multiplexer_7_out), .Q(out_4[6]));  // open: Qn, preset, reset
  Multiplexer #(.enable("false")) multiplexer_8 (.in0(out_4[7]), .in1(in_1[7]), .out(multiplexer_8_out), .sel(LOAD));
  D_Flip_Flop #(.trigger("falling")) d_ff_8 (
    .clk(CLK), .D(multiplexer_8_out), .Q(out_4[7]));  // open: Qn, preset, reset
  Multiplexer #(.enable("false")) multiplexer_9 (.in0(out_4[8]), .in1(in_1[8]), .out(multiplexer_9_out), .sel(LOAD));
  D_Flip_Flop #(.trigger("falling")) d_ff_9 (
    .clk(CLK), .D(multiplexer_9_out), .Q(out_4[8]));  // open: Qn, preset, reset
  Multiplexer #(.enable("false")) multiplexer_10 (.in0(out_4[9]), .in1(in_1[9]), .out(multiplexer_10_out), .sel(LOAD));
  D_Flip_Flop #(.trigger("falling")) d_ff_10 (
    .clk(CLK), .D(multiplexer_10_out), .Q(out_4[9]));  // open: Qn, preset, reset
  Multiplexer #(.enable("false")) multiplexer_11 (
    .in0(out_4[10]), .in1(in_1[10]), .out(multiplexer_11_out), .sel(LOAD));
  D_Flip_Flop #(.trigger("falling")) d_ff_11 (
    .clk(CLK), .D(multiplexer_11_out), .Q(out_4[10]));  // open: Qn, preset, reset
  D_Flip_Flop #(.trigger("falling")) d_ff_12 (
    .clk(CLK), .D(multiplexer_12_out), .Q(out_4[11]));  // open: Qn, preset, reset
  Multiplexer #(.enable("false")) multiplexer_12 (
    .in0(out_4[11]), .in1(in_1[11]), .out(multiplexer_12_out), .sel(LOAD));
  D_Flip_Flop #(.trigger("falling")) d_ff_13 (
    .clk(CLK), .D(multiplexer_13_out), .Q(out_4[12]));  // open: Qn, preset, reset
  Multiplexer #(.enable("false")) multiplexer_13 (
    .in0(out_4[12]), .in1(in_1[12]), .out(multiplexer_13_out), .sel(LOAD));
  Multiplexer #(.enable("false")) multiplexer_14 (
    .in0(out_4[13]), .in1(in_1[13]), .out(multiplexer_14_out), .sel(LOAD));
  D_Flip_Flop #(.trigger("falling")) d_ff_14 (
    .clk(CLK), .D(multiplexer_14_out), .Q(out_4[13]));  // open: Qn, preset, reset
  Multiplexer #(.enable("false")) multiplexer_15 (
    .in0(out_4[14]), .in1(in_1[14]), .out(multiplexer_15_out), .sel(LOAD));
  D_Flip_Flop #(.trigger("falling")) d_ff_15 (
    .clk(CLK), .D(multiplexer_15_out), .Q(out_4[14]));  // open: Qn, preset, reset
  Multiplexer #(.enable("false")) multiplexer_16 (
    .in0(out_4[15]), .in1(in_1[15]), .out(multiplexer_16_out), .sel(LOAD));
  D_Flip_Flop #(.trigger("falling")) d_ff_16 (
    .clk(CLK), .D(multiplexer_16_out), .Q(out_4[15]));  // open: Qn, preset, reset

  // Other names for the same wires on the sheet: B0 = in_1[0]; B1 = in_1[1]; B2 = in_1[2]; B3 = in_1[3]; B4 = in_1[4];
  //   B5 = in_1[5]; B6 = in_1[6]; B7 = in_1[7]; B8 = in_1[8]; B9 = in_1[9]; BA = in_1[10]; BB = in_1[11];
  //   BC = in_1[12]; BD = in_1[13]; BE = in_1[14]; BF = in_1[15]; M0 = out_4[0]; M1 = out_4[1]; M2 = out_4[2];
  //   M3 = out_4[3]; M4 = out_4[4]; M5 = out_4[5]; M6 = out_4[6]; M7 = out_4[7]; M8 = out_4[8]; M9 = out_4[9];
  //   MA = out_4[10]; MB = out_4[11]; MC = out_4[12]; MD = out_4[13]; ME = out_4[14]; MF = out_4[15]
endmodule

module Contador (
  input  CLK,
  input  CLEAR,
  output [7:0] out_3
);

  wire not_1_out, not_2_out, not_3_out, not_4_out, not_5_out, not_6_out, not_7_out;

  not not_1 (not_1_out, out_3[0]);
  T_Flip_Flop t_ff_1 (.clk(CLK), .T(1'b1), .Q(out_3[0]), .reset(CLEAR));  // open: Qn, preset
  T_Flip_Flop t_ff_2 (.clk(not_1_out), .T(1'b1), .Q(out_3[1]), .reset(CLEAR));  // open: Qn, preset
  not not_2 (not_2_out, out_3[1]);
  T_Flip_Flop t_ff_3 (.clk(not_2_out), .T(1'b1), .Q(out_3[2]), .reset(CLEAR));  // open: Qn, preset
  not not_3 (not_3_out, out_3[2]);
  T_Flip_Flop t_ff_4 (.clk(not_3_out), .T(1'b1), .Q(out_3[3]), .reset(CLEAR));  // open: Qn, preset
  not not_4 (not_4_out, out_3[3]);
  not not_5 (not_5_out, out_3[4]);
  T_Flip_Flop t_ff_5 (.clk(not_4_out), .T(1'b1), .Q(out_3[4]), .reset(CLEAR));  // open: Qn, preset
  T_Flip_Flop t_ff_6 (.clk(not_5_out), .T(1'b1), .Q(out_3[5]), .reset(CLEAR));  // open: Qn, preset
  not not_6 (not_6_out, out_3[5]);
  T_Flip_Flop t_ff_7 (.clk(not_6_out), .T(1'b1), .Q(out_3[6]), .reset(CLEAR));  // open: Qn, preset
  not not_7 (not_7_out, out_3[6]);
  T_Flip_Flop t_ff_8 (.clk(not_7_out), .T(1'b1), .Q(out_3[7]), .reset(CLEAR));  // open: Qn, preset

  // Other names for the same wires on the sheet: B0 = out_3[0]; B1 = out_3[1]; B2 = out_3[2]; B3 = out_3[3];
  //   B4 = out_3[4]; B5 = out_3[5]; B6 = out_3[6]; B7 = out_3[7]
endmodule

module Contador_Sincrono (
  input  CLK,
  input  CLEAR,
  output [7:0] out_3
);

  wire and_1_out, and_2_out, and_3_out, and_4_out, and_5_out, and_6_out;

  T_Flip_Flop t_ff_1 (.clk(CLK), .T(1'b1), .Q(out_3[0]), .reset(CLEAR));  // open: Qn, preset
  T_Flip_Flop t_ff_2 (.clk(CLK), .T(out_3[0]), .Q(out_3[1]), .reset(CLEAR));  // open: Qn, preset
  and and_1 (and_1_out, out_3[0], out_3[1]);
  T_Flip_Flop t_ff_3 (.clk(CLK), .T(and_1_out), .Q(out_3[2]), .reset(CLEAR));  // open: Qn, preset
  and and_2 (and_2_out, and_1_out, out_3[2]);
  and and_3 (and_3_out, and_2_out, out_3[3]);
  T_Flip_Flop t_ff_4 (.clk(CLK), .T(and_2_out), .Q(out_3[3]), .reset(CLEAR));  // open: Qn, preset
  and and_4 (and_4_out, and_3_out, out_3[4]);
  T_Flip_Flop t_ff_5 (.clk(CLK), .T(and_3_out), .Q(out_3[4]), .reset(CLEAR));  // open: Qn, preset
  T_Flip_Flop t_ff_6 (.clk(CLK), .T(and_4_out), .Q(out_3[5]), .reset(CLEAR));  // open: Qn, preset
  and and_5 (and_5_out, and_4_out, out_3[5]);
  T_Flip_Flop t_ff_7 (.clk(CLK), .T(and_5_out), .Q(out_3[6]), .reset(CLEAR));  // open: Qn, preset
  and and_6 (and_6_out, and_5_out, out_3[6]);
  T_Flip_Flop t_ff_8 (.clk(CLK), .T(and_6_out), .Q(out_3[7]), .reset(CLEAR));  // open: Qn, preset

  // Other names for the same wires on the sheet: B0 = out_3[0]; B1 = out_3[1]; B2 = out_3[2]; B3 = out_3[3];
  //   B4 = out_3[4]; B5 = out_3[5]; B6 = out_3[6]; B7 = out_3[7]
endmodule

module ROM_1 (
  input  [7:0] Addr,
  input  CLK,
  output [15:0] Data
);

  wire not_1_out;
  wire [15:0] ROM_256x16_data;

  ROM #(.dataWidth(16), .Select("low")) ROM_256x16 (.addr(Addr), .data(ROM_256x16_data));
  Register #(.width(16), .Select("low")) Reg16 (.D(ROM_256x16_data), .Q(Data), .clk(not_1_out));  // open: en, clr
  not not_1 (not_1_out, CLK);

  // Notes on the sheet:
  //   contents of ROM_256x16 (hex, n*v repeats v):
  //   6005 9101 6202 6304 c08 0 0 0 400 6001 9001 9002 6302 6102 9302 6200 6001 800
endmodule

module ROM_2 (
  input  [7:0] Addr,
  input  CLK,
  output [15:0] Data
);

  wire not_1_out;
  wire [15:0] ROM_256x16_data;

  Register #(.width(16), .Select("low")) Reg16 (.D(ROM_256x16_data), .Q(Data), .clk(not_1_out));  // open: en, clr
  ROM #(.dataWidth(16), .Select("low")) ROM_256x16 (.addr(Addr), .data(ROM_256x16_data));
  not not_1 (not_1_out, CLK);

  // Notes on the sheet:
  //   contents of ROM_256x16 (hex, n*v repeats v):
  //   6004 9102 6201 6305 9002 6002 9003 400 c0d 4*0 9002 6302 6101 9302 6200 6003 800
endmodule

module ULA (
  input  [3:0] A,
  input  [3:0] B,
  input  [1:0] S,
  output [3:0] out_4
);

  wire [3:0] adder_1_out, divider_1_out, multiplier_1_out, subtractor_1_out;

  Adder #(.width(4)) adder_1 (.a(A), .b(B), .out(adder_1_out));  // open: cin, cout
  Subtractor #(.width(4)) subtractor_1 (.a(A), .b(B), .out(subtractor_1_out));  // open: bin, bout
  Multiplier #(.width(4)) multiplier_1 (.a(A), .b(4'b0010), .out(multiplier_1_out));  // open: cin, cout
  Divider #(.width(4)) divider_1 (.a(4'b0010), .b(A), .out(divider_1_out));  // open: upper, rem
  Multiplexer #(.select(2), .width(4), .enable("false")) multiplexer_1 (
    .in0(adder_1_out), .in1(subtractor_1_out), .in2(multiplier_1_out), .in3(divider_1_out), .out(out_4),
    .sel(S));
endmodule
