// Logisim project CPU_entrega1.circ as structural Verilog: 2 circuits, main circuit Memória
module contador (
  output [8:0] out_1
);

  wire and_1_out, and_2_out, and_3_out, and_4_out, and_5_out, and_6_out, clock_1_out;

  Clock clock_1 (.out(clock_1_out));
  T_Flip_Flop t_ff_1 (.clk(clock_1_out), .T(1'b1), .Q(out_1[0]));  // open: Qn, preset, reset
  T_Flip_Flop t_ff_2 (.clk(clock_1_out), .T(out_1[0]), .Q(out_1[1]));  // open: Qn, preset, reset
  and and_1 (and_1_out, out_1[1], out_1[0]);
  T_Flip_Flop t_ff_3 (.clk(clock_1_out), .T(and_1_out), .Q(out_1[2]));  // open: Qn, preset, reset
  and and_2 (and_2_out, out_1[2], and_1_out);
  T_Flip_Flop t_ff_4 (.clk(clock_1_out), .T(and_2_out), .Q(out_1[3]));  // open: Qn, preset, reset
  and and_3 (and_3_out, out_1[3], and_2_out);
  T_Flip_Flop t_ff_5 (.clk(clock_1_out), .T(and_3_out), .Q(out_1[4]));  // open: Qn, preset, reset
  and and_4 (and_4_out, out_1[4], and_3_out);
  T_Flip_Flop t_ff_6 (.clk(clock_1_out), .T(and_4_out), .Q(out_1[5]));  // open: Qn, preset, reset
  and and_5 (and_5_out, out_1[5], and_4_out);
  T_Flip_Flop t_ff_7 (.clk(clock_1_out), .T(and_5_out), .Q(out_1[6]));  // open: Qn, preset, reset
  and and_6 (and_6_out, out_1[6], and_5_out);
  T_Flip_Flop t_ff_8 (.clk(clock_1_out), .T(and_6_out), .Q(out_1[7]));  // open: Qn, preset, reset

  assign out_1[8] = 1'b0;
endmodule

module \Memória  (
  input  [7:0] in_1
);

  wire clock_1_out;
  wire [15:0] rom_1_data;

  Clock clock_1 (.out(clock_1_out));
  ROM #(.dataWidth(16), .Select("low")) rom_1 (.addr(in_1), .data(rom_1_data), .sel(clock_1_out));

  // Notes on the sheet:
  //   contents of rom_1 (hex, n*v repeats v):
  //   10 0 0 1 1 1 0 1 10 10 0 10 10 11 22*0 10 0 0 1 1 0 0 1 1 0 0 10 10 11 0 10 10 1 0 10 1 11 0 10 10
  //   10 0 0 10 0 0 1
endmodule
