// Logisim project contador2_0.circ as structural Verilog: 1 circuit, main circuit main
module main (
  output [8:0] out_1
);

  wire C1, K0, K1, K2, K3, L0, L1, L2, L3, L4, L5, L6, L7, L8, L9, not_1_out, not_2_out, not_3_out,
       not_4_out, not_5_out, not_6_out, not_7_out, S0, S1, S2, S3, S4, S5, S6, S7, S8, S9;
  wire [3:0] HEX2, HEX3, HEX4, HEX5;

  Hex_Digit_Display hex_digit_display_1 (.value(HEX5));  // open: dp
  LED u_L9 (.in(L9));
  LED u_L8 (.in(L8));
  // DipSwitch #(.NSwitches(1)) S9: pin names not known; wires that end beside it: S9
  // DipSwitch #(.NSwitches(1)) S8: pin names not known; wires that end beside it: S8
  Hex_Digit_Display hex_digit_display_2 (.value(HEX3));  // open: dp
  Hex_Digit_Display hex_digit_display_3 (.value(HEX4));  // open: dp
  LED u_L6 (.in(L6));
  LED u_L7 (.in(L7));
  LED u_L5 (.in(L5));
  // DipSwitch #(.NSwitches(1)) S5: pin names not known; wires that end beside it: S5
  // DipSwitch #(.NSwitches(1)) S6: pin names not known; wires that end beside it: S6, C1
  // DipSwitch #(.NSwitches(1)) S7: pin names not known; wires that end beside it: S7
  Hex_Digit_Display hex_digit_display_4 (.value(HEX2));  // open: dp
  LED u_L4 (.in(L4));
  LED u_L3 (.in(L3));
  // DipSwitch #(.NSwitches(1)) S2: pin names not known; wires that end beside it: S2
  // DipSwitch #(.NSwitches(1)) S3: pin names not known; wires that end beside it: S3
  // DipSwitch #(.NSwitches(1)) S4: pin names not known; wires that end beside it: S4
  T_Flip_Flop t_ff_1 (.clk(C1), .T(1'b1), .Q(out_1[0]));  // open: Qn, preset, reset
  not not_1 (not_1_out, out_1[0]);
  Hex_Digit_Display hex_digit_display_5 (.value(out_1[7:4]));  // open: dp
  Hex_Digit_Display hex_digit_display_6 (.value(out_1[3:0]));  // open: dp
  LED u_L1 (.in(L1));
  LED u_L0 (.in(L0));
  LED u_L2 (.in(L2));
  // DipSwitch #(.NSwitches(1)) S0: pin names not known; wires that end beside it: S0
  // DipSwitch #(.NSwitches(1)) S1: pin names not known; wires that end beside it: S1
  T_Flip_Flop t_ff_2 (.clk(not_1_out), .T(1'b1), .Q(out_1[1]));  // open: Qn, preset, reset
  not not_2 (not_2_out, out_1[1]);
  Button u_K3 (.out(K3));
  Button u_K2 (.out(K2));
  not not_3 (not_3_out, out_1[2]);
  T_Flip_Flop t_ff_3 (.clk(not_2_out), .T(1'b1), .Q(out_1[2]));  // open: Qn, preset, reset
  Clock clock_1 (.out(C1));
  Button u_K0 (.out(K0));
  Button u_K1 (.out(K1));
  T_Flip_Flop t_ff_4 (.clk(not_3_out), .T(1'b1), .Q(out_1[3]));  // open: Qn, preset, reset
  not not_4 (not_4_out, out_1[3]);
  not not_5 (not_5_out, out_1[4]);
  T_Flip_Flop t_ff_5 (.clk(not_4_out), .T(1'b1), .Q(out_1[4]));  // open: Qn, preset, reset
  not not_6 (not_6_out, out_1[5]);
  T_Flip_Flop t_ff_6 (.clk(not_5_out), .T(1'b1), .Q(out_1[5]));  // open: Qn, preset, reset
  not not_7 (not_7_out, out_1[6]);
  T_Flip_Flop t_ff_7 (.clk(not_6_out), .T(1'b1), .Q(out_1[6]));  // open: Qn, preset, reset
  T_Flip_Flop t_ff_8 (.clk(not_7_out), .T(1'b1), .Q(out_1[7]));  // open: Qn, preset, reset
  // Digital_Oscilloscope digital_oscilloscope_1: pin names not known; wires that end beside it: C1, out_1[0], out_1[1], out_1[2], out_1[3], out_1[4], out_1[5], out_1[6], out_1[7], K0

  assign out_1[8] = 1'b0;

  // Other names for the same wires on the sheet: B0 = out_1[0]; HEX0[3:0] = out_1[3:0]; B1 = out_1[1]; B2 = out_1[2];
  //   B3 = out_1[3]; B4 = out_1[4]; HEX1[3:0] = out_1[7:4]; B5 = out_1[5]; B6 = out_1[6]; B7 = out_1[7]
endmodule
