// Logisim project CPU_ULA_minha.circ as structural Verilog: 6 circuits, main circuit CPU
// CLK
module CPU (
);

  wire Clock, K0, K1, K2, K3, L8, L9, S0, S1, S2, S3, S4, S5, S6, S7, S8;
  wire [3:0] HEX0, HEX1, HEX2, HEX3, HEX4, HEX5;
  wire [7:0] A1;

  Hex_Digit_Display hex_digit_display_1 (.value(HEX5));  // open: dp
  LED u_L9 (.in(L9));
  LED u_L8 (.in(L8));
  // DipSwitch #(.NSwitches(1)) S8: pin names not known; wires that end beside it: S8
  // DipSwitch #(.NSwitches(1)) S9: pin names not known; wires that end beside it: Clock
  // Digital_Oscilloscope digital_oscilloscope_1: pin names not known; wires that end beside it: Clock, A1[0], A1[1], A1[2], A1[3], A1[4], A1[5], A1[6], A1[7], K0
  Hex_Digit_Display hex_digit_display_2 (.value(HEX3));  // open: dp
  Hex_Digit_Display hex_digit_display_3 (.value(HEX4));  // open: dp
  LED L6 (.in(A1[6]));
  LED L5 (.in(A1[5]));
  LED L7 (.in(A1[7]));
  // DipSwitch #(.NSwitches(1)) S5: pin names not known; wires that end beside it: S5
  // DipSwitch #(.NSwitches(1)) S6: pin names not known; wires that end beside it: S6
  // DipSwitch #(.NSwitches(1)) S7: pin names not known; wires that end beside it: S7
  Hex_Digit_Display hex_digit_display_4 (.value(HEX2));  // open: dp
  LED L4 (.in(A1[4]));
  LED L3 (.in(A1[3]));
  // DipSwitch #(.NSwitches(1)) S2: pin names not known; wires that end beside it: S2
  // DipSwitch #(.NSwitches(1)) S4: pin names not known; wires that end beside it: S4
  // DipSwitch #(.NSwitches(1)) S3: pin names not known; wires that end beside it: S3
  Hex_Digit_Display hex_digit_display_5 (.value(HEX0));  // open: dp
  Hex_Digit_Display hex_digit_display_6 (.value(HEX1));  // open: dp
  LED L2 (.in(A1[2]));
  LED L1 (.in(A1[1]));
  LED L0 (.in(A1[0]));
  // DipSwitch #(.NSwitches(1)) S1: pin names not known; wires that end beside it: S1
  // DipSwitch #(.NSwitches(1)) M_CLR: pin names not known; wires that end beside it: S0, Clock
  Button u_K2 (.out(K2));
  Button u_K3 (.out(K3));
  Button Reset2 (.out(K1));
  Button Reset1 (.out(K0));
  Registrador registrador_1 ();  // open: Load, Dados, CLK, CLR, Q
  ULA ula_1 ();  // open: Operando, RgIN, ULA, RgTO
  Registrador registrador_2 ();  // open: Load, Dados, CLK, CLR, Q
  Contador_Sincrono contador_sincrono_1 (.CLK(Clock), .CLEAR(S0), .out_3(A1));
  ROM #(.dataWidth(16), .Select("low")) rom_1 (.addr(A1), .data({HEX5, HEX4, HEX3, HEX2}));

  // Other names for the same wires on the sheet: L0 = A1[0]; L1 = A1[1]; L2 = A1[2]; L3 = A1[3]; L4 = A1[4];
  //   L5 = A1[5]; L6 = A1[6]; L7 = A1[7]; S9 = Clock

  // Notes on the sheet:
  //   contents of rom_1 (hex, n*v repeats v):
  //   10 0 0 1 1 1 0 1 10 10 0 10 10 11 22*0 10 0 0 1 1 0 0 1 1 0 0 10 10 11 0 10 10 1 0 10 1 11 0 10 10
  //   10 0 0 10 0 0 1
endmodule

module Contador (
  input  CLK,
  input  CLEAR,
  output [7:0] out_3
);

  wire not_1_out, not_2_out, not_3_out, not_4_out, not_5_out, not_6_out, not_7_out;

  not not_1 (not_1_out, out_3[0]);
  T_Flip_Flop t_ff_1 (.clk(CLK), .T(1'b1), .Q(out_3[0]), .reset(CLEAR));  // open: Qn, preset
  not not_2 (not_2_out, out_3[1]);
  T_Flip_Flop t_ff_2 (.clk(not_1_out), .T(1'b1), .Q(out_3[1]), .reset(CLEAR));  // open: Qn, preset
  T_Flip_Flop t_ff_3 (.clk(not_2_out), .T(1'b1), .Q(out_3[2]), .reset(CLEAR));  // open: Qn, preset
  not not_3 (not_3_out, out_3[2]);
  not not_4 (not_4_out, out_3[3]);
  T_Flip_Flop t_ff_4 (.clk(not_3_out), .T(1'b1), .Q(out_3[3]), .reset(CLEAR));  // open: Qn, preset
  not not_5 (not_5_out, out_3[4]);
  T_Flip_Flop t_ff_5 (.clk(not_4_out), .T(1'b1), .Q(out_3[4]), .reset(CLEAR));  // open: Qn, preset
  not not_6 (not_6_out, out_3[5]);
  T_Flip_Flop t_ff_6 (.clk(not_5_out), .T(1'b1), .Q(out_3[5]), .reset(CLEAR));  // open: Qn, preset
  T_Flip_Flop t_ff_7 (.clk(not_6_out), .T(1'b1), .Q(out_3[6]), .reset(CLEAR));  // open: Qn, preset
  not not_7 (not_7_out, out_3[6]);
  T_Flip_Flop t_ff_8 (.clk(not_7_out), .T(1'b1), .Q(out_3[7]), .reset(CLEAR));  // open: Qn, preset

  // Other names for the same wires on the sheet: B0 = out_3[0]; B1 = out_3[1]; B2 = out_3[2]; B3 = out_3[3];
  //   B4 = out_3[4]; B5 = out_3[5]; B6 = out_3[6]; B7 = out_3[7]
endmodule

module Contador_Sincrono (
  input  CLK,
  input  CLEAR,
  output [7:0] out_3
);

  wire and_1_out, and_2_out, and_3_out, and_4_out, and_5_out, and_6_out;

  T_Flip_Flop t_ff_1 (.clk(CLK), .T(1'b1), .Q(out_3[0]), .reset(CLEAR));  // open: Qn, preset
  T_Flip_Flop t_ff_2 (.clk(CLK), .T(out_3[0]), .Q(out_3[1]), .reset(CLEAR));  // open: Qn, preset
  and and_1 (and_1_out, out_3[0], out_3[1]);
  T_Flip_Flop t_ff_3 (.clk(CLK), .T(and_1_out), .Q(out_3[2]), .reset(CLEAR));  // open: Qn, preset
  and and_2 (and_2_out, and_1_out, out_3[2]);
  and and_3 (and_3_out, and_2_out, out_3[3]);
  T_Flip_Flop t_ff_4 (.clk(CLK), .T(and_2_out), .Q(out_3[3]), .reset(CLEAR));  // open: Qn, preset
  and and_4 (and_4_out, and_3_out, out_3[4]);
  T_Flip_Flop t_ff_5 (.clk(CLK), .T(and_3_out), .Q(out_3[4]), .reset(CLEAR));  // open: Qn, preset
  T_Flip_Flop t_ff_6 (.clk(CLK), .T(and_4_out), .Q(out_3[5]), .reset(CLEAR));  // open: Qn, preset
  and and_5 (and_5_out, and_4_out, out_3[5]);
  T_Flip_Flop t_ff_7 (.clk(CLK), .T(and_5_out), .Q(out_3[6]), .reset(CLEAR));  // open: Qn, preset
  and and_6 (and_6_out, and_5_out, out_3[6]);
  T_Flip_Flop t_ff_8 (.clk(CLK), .T(and_6_out), .Q(out_3[7]), .reset(CLEAR));  // open: Qn, preset

  // Other names for the same wires on the sheet: B0 = out_3[0]; B1 = out_3[1]; B2 = out_3[2]; B3 = out_3[3];
  //   B4 = out_3[4]; B5 = out_3[5]; B6 = out_3[6]; B7 = out_3[7]
endmodule

module Memoria_1 (
  input  [7:0] Addr,
  input  CLK,
  output [15:0] Data
);

  wire not_1_out;
  wire [15:0] ROM_256x16_data;

  Register #(.width(16), .Select("low")) Reg16 (.D(ROM_256x16_data), .Q(Data), .clk(not_1_out));  // open: en, clr
  ROM #(.dataWidth(16), .Select("low")) ROM_256x16 (.addr(Addr), .data(ROM_256x16_data));
  not not_1 (not_1_out, CLK);

  // Notes on the sheet:
  //   contents of ROM_256x16 (hex, n*v repeats v):
  //   10 0 0 1 1 1 0 1 10 10 0 10 10 11 22*0 10 0 0 1 1 0 0 1 1 0 0 10 10 11 0 10 10 1 0 10 1 11 0 10 10
  //   10 0 0 10 0 0 1
endmodule

module ULA (
  input  [3:0] Operando,
  input  [3:0] RgIN,
  input  [1:0] ULA,
  output [3:0] RgTO
);

  wire [3:0] adder_1_out, divider_1_out, multiplier_1_out, subtractor_1_out;

  Adder #(.width(4)) adder_1 (.a(Operando), .b(RgIN), .out(adder_1_out));  // open: cin, cout
  Subtractor #(.width(4)) subtractor_1 (.a(Operando), .b(RgIN), .out(subtractor_1_out));  // open: bin, bout
  Multiplier #(.width(4)) multiplier_1 (.a(Operando), .b(4'b0010), .out(multiplier_1_out));  // open: cin, cout
  Divider #(.width(4)) divider_1 (.a(4'b0010), .b(Operando), .out(divider_1_out));  // open: upper, rem
  Multiplexer #(.select(2), .width(4), .enable("false")) multiplexer_1 (
    .in0(adder_1_out), .in1(subtractor_1_out), .in2(multiplier_1_out), .in3(divider_1_out), .out(RgTO),
    .sel(ULA));
endmodule

// Reg4
module Registrador (
  input  Load,
  input  [3:0] Dados,
  input  CLK,
  input  CLR,
  output [3:0] Q
);

  wire and_1_out, multiplexer_1_out, multiplexer_2_out, multiplexer_3_out, multiplexer_4_out;

  Multiplexer #(.enable("false")) multiplexer_1 (.in0(Q[3]), .in1(Dados[3]), .out(multiplexer_1_out), .sel(Load));
  and and_1 (and_1_out, CLK, CLR);
  D_Flip_Flop d_ff_1 (.clk(CLK), .D(multiplexer_1_out), .Q(Q[3]), .reset(and_1_out));  // open: Qn, preset
  Multiplexer #(.enable("false")) multiplexer_2 (.in0(Q[2]), .in1(Dados[2]), .out(multiplexer_2_out), .sel(Load));
  D_Flip_Flop d_ff_2 (.clk(CLK), .D(multiplexer_2_out), .Q(Q[2]), .reset(and_1_out));  // open: Qn, preset
  Multiplexer #(.enable("false")) multiplexer_3 (.in0(Q[1]), .in1(Dados[1]), .out(multiplexer_3_out), .sel(Load));
  D_Flip_Flop d_ff_3 (.clk(CLK), .D(multiplexer_3_out), .Q(Q[1]), .reset(and_1_out));  // open: Qn, preset
  Multiplexer #(.enable("false")) multiplexer_4 (.in0(Q[0]), .in1(Dados[0]), .out(multiplexer_4_out), .sel(Load));
  D_Flip_Flop d_ff_4 (.clk(CLK), .D(multiplexer_4_out), .Q(Q[0]), .reset(and_1_out));  // open: Qn, preset
endmodule
